// Logisim project day1_logic.circ as structural Verilog: 3 circuits, main circuit main
module main (
  input  a,
  input  b,
  input  in_3,
  input  in_4,
  input  in_5,
  output out_6
);

  wire and_1_out, and_2_out, and_3_out;

  // XOR_Gate xor_1 is placed but not wired
  and and_1 (and_1_out, b, ~a);  // AND_Gate
  and and_2 (and_2_out, ~b, a);  // AND_Gate
  or or_1 (out_6, and_1_out, and_2_out);
  and and_3 (and_3_out, in_3, in_4, in_5);
endmodule

module OneBitAdder (
  input  a,
  input  b,
  input  c,
  output s,
  output cout
);

  wire AB_out, AC_out, BC_out;

  and AB (AB_out, b, a);
  and BC (BC_out, c, b);
  and AC (AC_out, c, a);
  xor xor_1 (s, c, b, a);
  or or_1 (cout, AB_out, BC_out, AC_out);
endmodule

module FourBitAdder (
);

  OneBitAdder onebitadder_1 ();  // open: a, b, c, s, cout
  OneBitAdder onebitadder_2 ();  // open: a, b, c, s, cout
  OneBitAdder onebitadder_3 ();  // open: a, b, c, s, cout
  OneBitAdder onebitadder_4 ();  // open: a, b, c, s, cout
endmodule
